# Fritzing sketch cablage_arduino (saved by Fritzing 0.9.1b)

parts:
  NEOPIXEL1 = Neopixel Strip -- White (30/m)
  Composant1 = Arduino Ethernet Shield (Rev3)
  Zone1 = Neopixel Strip -- White (30/m)
  NEOPIXEL2 = Neopixel Strip -- White (30/m) [part_number=1376]
  NEOPIXEL3 = Neopixel Strip -- White (30/m) [part_number=1376]
  NEOPIXEL4 = Neopixel Strip -- White (30/m) [part_number=1376]
  NEOPIXEL5 = Neopixel Strip -- White (30/m) [part_number=1376]

nets:
  GND: NEOPIXEL1.GND, Composant1.GND, Zone1.GND, NEOPIXEL2.GND#1, NEOPIXEL4.GND#1
  N1: NEOPIXEL1.Din, Composant1.PWM_D9
  5V: Composant1.5V, Zone1.+5V
  N2: Composant1.PWM_D3, Zone1.Din
  N3: Composant1.PWM_D5, NEOPIXEL2.Din
  N4: Composant1.PWM_D6, NEOPIXEL4.Din
  N5: NEOPIXEL2.+5V#4, NEOPIXEL3.+5V
  N6: NEOPIXEL2.Dout, NEOPIXEL3.Din
  N7: NEOPIXEL2.GND#6, NEOPIXEL3.GND
  N8: NEOPIXEL4.+5V#4, NEOPIXEL5.+5V
  N9: NEOPIXEL4.Dout, NEOPIXEL5.Din
  N10: NEOPIXEL4.GND#6, NEOPIXEL5.GND

custom parts:
  Neopixel Strip -- White (30/m): These NeoPixel strips have 30 digitally-addressable pixel LEDs per meter and are very affordable and are only 12.5 mm wide, 10 mm if you remove the strip from the casing.
